# Fritzing sketch diagram (saved by Fritzing 0.9.3b)
breadboards: 1

parts:
  S1 = Pushbutton [package="[THT]"]
  Part1 = Arduino Nano (Rev3.0)
  R1 = Resistor [tolerance=±5% resistance=220 package=THT]
  LED1 = LED - 5mm [color="Red (633nm)" package="5 mm [THT]"]
  R2 = Resistor [tolerance=±5% resistance=220 package=THT]

nets:
  N1: S1.Pin_1, S1.Pin_2, Part1.D2, R1.Pin_1
  N2: S1.Pin_3, S1.Pin_4, Part1.5V
  N3: Part1.GND, R1.Pin_0, R2.Pin_0
  N4: Part1.D12/MISO, LED1.anode
  N5: LED1.cathode, R2.Pin_1
