# Fritzing sketch arduino1 (saved by Fritzing 0.9.3b)
breadboards: 1

parts:
  U1 = atmega328 [package=dip]
  Y1 = CRYSTAL [package=crystal-smd-10.5x4.8-2pin]
  C1 = Capacitor [package=cap-pth-small2]
  R1 = Resistor [tolerance=±5% resistance=10k package="2512 [SMD]"]
  C2 = Capacitor [package=1210]
  S1 = SWITCH-MOMENTARY-2 [package=tactile-pth]

nets:
  N1: U1.RESET, R1.Pin_1, S1.2
  5V: U1.VCC, R1.Pin_0
  GND: U1.GND#7, C1.1, C2.1, S1.1
  N2: U1.XLAT1, Y1.1, C1.2
  N3: U1.XLAT2, Y1.2, C2.2
